# Fritzing sketch wiring-rainbowWarrior-breadboard (saved by Fritzing 0.9.2b)
breadboards: 1

parts:
  U1 = ESP32S-HiLetgo [part_number=ESP32S-HiLetgo]
  R1 = Resistor [tolerance=±5% resistance=1k package=THT]
  R2 = Photocell (LDR) [package=THT]
  J1 = Piezo Speaker
  U2 = Tri-Color LED SMD [package=led-tricolor-smd]

nets:
  N1: U1.3.3, R2.pin_0
  N2: U1.GPIO36, R1.Pin_1, R2.pin_1
  N3: U1.GND, R1.Pin_0, J1.pin1, U2.GRN
  N4: U1.VIN, U2.RED
  N5: U1.GPIO22, J1.pin2

custom parts:
  ESP32S-HiLetgo: HiLetgo ESP-WROOM-32 ESP32 ESP-32S Development Board 2.4GHz Dual-Mode WiFi + Bluetooth Dual Cores Microcontroller The ESP32 integrated with Antenna switches, RF Balun, power amplifiers, low-noise amplifiers, filters, and management modules, and the entire solution occupies the least area of PCB. 2.4 GHz Wi-Fi plus Bluetooth dual-mode chip, with TSMC Ultra-low power consumption 40nm technology,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
